// Logisim project macinstallbackground.circ as structural Verilog
module main (
  input  in_1,
  input  in_2,
  output out_3
);

  wire and_1_out, and_2_out, not_1_out, not_2_out;

  arrow arrow_1 ();
  not not_1 (not_1_out, in_1);
  and and_1 (and_1_out, not_1_out, in_2);
  and and_2 (and_2_out, in_1, not_2_out);
  not not_2 (not_2_out, in_2);
  or or_1 (out_3, and_1_out, and_2_out);

  // Notes on the sheet:
  //   Logisim Evolution
  //   To install, drag the icon 
  //   into your Applications folder.
  //   version 2.13.18
  //   Holy Cross Edition
endmodule
